// Logisim project 19bits_MIPS_Circuit.circ as structural Verilog: 6 circuits, main circuit ALU_19_Bits
module ALU_19_Bits (
  input  [18:0] A,
  input  [18:0] B,
  input  [3:0] ShiftAmnt,
  input  [2:0] ALUop,
  output [18:0] Result,
  output Zero
);

  wire [4:0] bit_extender_1_out;
  wire [18:0] adder_1_out, adder_2_out, shifter_1_out, shifter_2_out, subtractor_1_out, xor_1_out;

  assign bit_extender_1_out = {{1{1'b0}}, ShiftAmnt};  // Bit_Extender bit_extender_1
  Adder #(.width(19)) adder_1 (.a(A), .b(B), .out(adder_1_out));  // open: cin, cout
  Subtractor #(.width(19)) subtractor_1 (.a(A), .b(B), .out(subtractor_1_out));  // open: bin, bout
  Adder #(.width(19)) adder_2 (.a(A), .b(19'h1), .out(adder_2_out));  // open: cin, cout
  Shifter #(.width(19)) shifter_1 (.in(A), .\dist (bit_extender_1_out), .out(shifter_1_out));
  Shifter #(.shift("lr"), .width(19)) shifter_2 (.in(A), .\dist (bit_extender_1_out), .out(shifter_2_out));
  assign xor_1_out = A ^ B;  // XOR_Gate xor_1, 19 bits wide
  Multiplexer #(.select(3), .width(19)) multiplexer_1 (
    .in0(adder_1_out), .in1(subtractor_1_out), .in2(adder_2_out), .in3(shifter_1_out), .in4(shifter_2_out),
    .in5(xor_1_out), .out(Result), .sel(ALUop));  // open: in6, in7
  nor nor_1 (Zero, Result[0], Result[1], Result[2], Result[3], Result[4], Result[5], Result[6], Result[7], Result[8], Result[9], Result[10], Result[11], Result[12], Result[13], Result[14], Result[15], Result[16], Result[17], Result[18]);

  // Notes on the sheet:
  //   Design: ALU-19 Bit
  //   OperationName         |            OpCode
  //   ADD            |            000
  //   SUB            |           001
  //   INC            |            010
  //   SHL            |            011
  //   SHR            |            100
  //   XOR            |            101
endmodule

module ALU_Test (
  input  [2:0] in_1,
  input  [18:0] in_2,
  input  [3:0] in_3,
  input  [18:0] in_4,
  output out_5,
  output [18:0] out_6
);

  ALU_19_Bits alu_19_bits_1 (.ShiftAmnt(in_3), .ALUop(in_1), .A(in_2), .B(in_4), .Result(out_6), .Zero(out_5));

  // Notes on the sheet:
  //   OperationName         |            OpCode
  //   ADD            |            000
  //   SUB            |           001
  //   INC            |            010
  //   SHL            |            011
  //   SHR            |            100
  //   XOR            |            101
endmodule

module Datapath (
  input  in_1
);

  wire alu_19_bits_1_zero, and_1_out, clock_1_out, control_unit_1_alusrc, control_unit_1_branch,
       control_unit_1_jump, control_unit_1_memread, control_unit_1_memtoreg, control_unit_1_memwrite,
       control_unit_1_regdest, control_unit_1_regwrite;
  wire [2:0] control_unit_1_aluop;
  wire [3:0] multiplexer_3_out, rom_1_data_2, rom_1_data_3, rom_1_data_4, rom_1_data_5;
  wire [18:0] adder_1_out, alu_19_bits_1_result, bit_extender_1_out, bit_extender_2_out, multiplexer_1_out,
       multiplexer_2_out, multiplexer_4_out, multiplexer_5_out, Program_Counter_q, ram_1_dout,
       register_bit_19_1_read_data1, register_bit_19_1_read_data2;
  wire [18:16] rom_1_data;

  assign bit_extender_1_out = {{3{1'b0}}, {rom_1_data_4, rom_1_data_5, rom_1_data_3, rom_1_data_2}};  // Bit_Extender bit_extender_1
  Multiplexer #(.width(19)) multiplexer_1 (
    .in0(adder_1_out), .in1(bit_extender_1_out), .out(multiplexer_1_out), .sel(control_unit_1_jump));
  and and_1 (and_1_out, alu_19_bits_1_zero, control_unit_1_branch);
  Multiplexer #(.width(19)) multiplexer_2 (
    .in0(multiplexer_1_out), .in1(bit_extender_2_out), .out(multiplexer_2_out), .sel(and_1_out));
  Register #(.width(19)) Program_Counter (
    .D(multiplexer_2_out), .en(in_1), .clk(clock_1_out), .Q(Program_Counter_q));  // open: clr
  Clock clock_1 (.out(clock_1_out));
  Adder #(.width(19)) adder_1 (.a(19'h1), .b(Program_Counter_q), .out(adder_1_out));  // open: cin, cout
  ROM #(.addrWidth(19), .dataWidth(19)) rom_1 (
    .addr(Program_Counter_q), .data({rom_1_data, rom_1_data_4, rom_1_data_5, rom_1_data_3, rom_1_data_2}));
  Multiplexer #(.width(4)) multiplexer_3 (
    .in0(rom_1_data_3), .in1(rom_1_data_5), .out(multiplexer_3_out), .sel(control_unit_1_regdest));
  Control_Unit control_unit_1 (
    .OpCode(rom_1_data), .ALUSrc(control_unit_1_alusrc), .RegDest(control_unit_1_regdest),
    .RegWrite(control_unit_1_regwrite), .MemToReg(control_unit_1_memtoreg), .MemRead(control_unit_1_memread),
    .MemWrite(control_unit_1_memwrite), .Jump(control_unit_1_jump), .Branch(control_unit_1_branch),
    .ALUop(control_unit_1_aluop));
  Register_Bit_19 register_bit_19_1 (
    .Read_Address1(rom_1_data_4), .Write_Address(multiplexer_3_out), .Read_Address2(rom_1_data_5),
    .ClK(clock_1_out), .Write(control_unit_1_regwrite), .Write_Data(multiplexer_5_out),
    .Read_Data1(register_bit_19_1_read_data1), .Read_Data2(register_bit_19_1_read_data2));
  assign bit_extender_2_out = {{11{1'b0}}, {rom_1_data_3, rom_1_data_2}};  // Bit_Extender bit_extender_2
  Multiplexer #(.width(19)) multiplexer_4 (
    .in0(register_bit_19_1_read_data2), .in1(bit_extender_2_out), .out(multiplexer_4_out),
    .sel(control_unit_1_alusrc));
  Multiplexer #(.width(19)) multiplexer_5 (
    .in0(alu_19_bits_1_result), .in1(ram_1_dout), .out(multiplexer_5_out), .sel(control_unit_1_memtoreg));
  ALU_19_Bits alu_19_bits_1 (
    .ShiftAmnt(rom_1_data_2), .ALUop(control_unit_1_aluop), .A(register_bit_19_1_read_data1),
    .B(multiplexer_4_out), .Result(alu_19_bits_1_result), .Zero(alu_19_bits_1_zero));
  RAM #(.addrWidth(19), .asyncread("true"), .dataWidth(19)) ram_1 (
    .addr(alu_19_bits_1_result), .we(control_unit_1_memwrite), .oe(control_unit_1_memread),
    .clk(clock_1_out), .din(register_bit_19_1_read_data2), .dout(ram_1_dout));

  // Notes on the sheet:
  //   contents of rom_1 (hex, n*v repeats v):
  //   11110 12220 2220a 13330 14440 23305 54300 1310 24401 6240b 70005 7000b
  //   Datapath of 19 bit processor
endmodule

module Register_Bit_19 (
  input  [18:0] Write_Data,
  input  ClK,
  input  Write,
  input  [3:0] Write_Address,
  input  [3:0] Read_Address1,
  input  [3:0] Read_Address2,
  output [18:0] Read_Data1,
  output [18:0] Read_Data2
);

  wire decoder_1_out0, decoder_1_out1, decoder_1_out2, decoder_1_out3, decoder_1_out4, decoder_1_out5,
       decoder_1_out6, decoder_1_out7, decoder_1_out8, decoder_1_out9, decoder_1_out10, decoder_1_out11,
       decoder_1_out12, decoder_1_out13, decoder_1_out14, decoder_1_out15;
  wire [18:0] R0_q, R1_q, R2_q, R3_q, R4_q, R5_q, R6_q, R7_q, R8_q, R9_q, R10_q, R11_q, R12_q, R13_q, R14_q,
       R15_q;

  Decoder #(.select(4)) decoder_1 (
    .out0(decoder_1_out0), .out1(decoder_1_out1), .out2(decoder_1_out2), .out3(decoder_1_out3),
    .out4(decoder_1_out4), .out5(decoder_1_out5), .out6(decoder_1_out6), .out7(decoder_1_out7),
    .out8(decoder_1_out8), .out9(decoder_1_out9), .out10(decoder_1_out10), .out11(decoder_1_out11),
    .out12(decoder_1_out12), .out13(decoder_1_out13), .out14(decoder_1_out14), .out15(decoder_1_out15),
    .sel(Write_Address), .en(Write));
  Register #(.width(19)) R0 (.D(Write_Data), .en(decoder_1_out0), .clk(ClK), .Q(R0_q));  // open: clr
  Register #(.width(19)) R3 (.D(Write_Data), .en(decoder_1_out3), .clk(ClK), .Q(R3_q));  // open: clr
  Register #(.width(19)) R4 (.D(Write_Data), .en(decoder_1_out4), .clk(ClK), .Q(R4_q));  // open: clr
  Register #(.width(19)) R5 (.D(Write_Data), .en(decoder_1_out5), .clk(ClK), .Q(R5_q));  // open: clr
  Register #(.width(19)) R6 (.D(Write_Data), .en(decoder_1_out6), .clk(ClK), .Q(R6_q));  // open: clr
  Register #(.width(19)) R7 (.D(Write_Data), .en(decoder_1_out7), .clk(ClK), .Q(R7_q));  // open: clr
  Register #(.width(19)) R1 (.D(Write_Data), .en(decoder_1_out1), .clk(ClK), .Q(R1_q));  // open: clr
  Register #(.width(19)) R2 (.D(Write_Data), .en(decoder_1_out2), .clk(ClK), .Q(R2_q));  // open: clr
  Register #(.width(19)) R8 (.D(Write_Data), .en(decoder_1_out8), .clk(ClK), .Q(R8_q));  // open: clr
  Register #(.width(19)) R9 (.D(Write_Data), .en(decoder_1_out9), .clk(ClK), .Q(R9_q));  // open: clr
  Register #(.width(19)) R10 (.D(Write_Data), .en(decoder_1_out10), .clk(ClK), .Q(R10_q));  // open: clr
  Register #(.width(19)) R11 (.D(Write_Data), .en(decoder_1_out11), .clk(ClK), .Q(R11_q));  // open: clr
  Register #(.width(19)) R12 (.D(Write_Data), .en(decoder_1_out12), .clk(ClK), .Q(R12_q));  // open: clr
  Register #(.width(19)) R13 (.D(Write_Data), .en(decoder_1_out13), .clk(ClK), .Q(R13_q));  // open: clr
  Register #(.width(19)) R14 (.D(Write_Data), .en(decoder_1_out14), .clk(ClK), .Q(R14_q));  // open: clr
  Register #(.width(19)) R15 (.D(Write_Data), .en(decoder_1_out15), .clk(ClK), .Q(R15_q));  // open: clr
  Multiplexer #(.select(4), .width(19)) multiplexer_1 (
    .in0(R0_q), .in1(R1_q), .in2(R2_q), .in3(R3_q), .in4(R4_q), .in5(R5_q), .in6(R6_q), .in7(R7_q),
    .in8(R8_q), .in9(R9_q), .in10(R10_q), .in11(R11_q), .in12(R12_q), .in13(R13_q), .in14(R14_q),
    .in15(R15_q), .out(Read_Data1), .sel(Read_Address1));
  Multiplexer #(.select(4), .width(19)) multiplexer_2 (
    .in0(R0_q), .in1(R1_q), .in2(R2_q), .in3(R3_q), .in4(R4_q), .in5(R5_q), .in6(R6_q), .in7(R7_q),
    .in8(R8_q), .in9(R9_q), .in10(R10_q), .in11(R11_q), .in12(R12_q), .in13(R13_q), .in14(R14_q),
    .in15(R15_q), .out(Read_Data2), .sel(Read_Address2));

  // Notes on the sheet:
  //   Design of Registers 19 bits each
endmodule

module Register_Test (
  input  [3:0] in_1,
  input  [3:0] in_2,
  input  [3:0] in_3,
  input  [18:0] in_4,
  input  in_5,
  output [18:0] out_6,
  output [18:0] out_7
);

  wire clock_1_out;

  Clock clock_1 (.out(clock_1_out));
  Register_Bit_19 register_bit_19_1 (
    .Read_Address1(in_1), .Write_Address(in_3), .Read_Address2(in_2), .ClK(clock_1_out), .Write(in_5),
    .Write_Data(in_4), .Read_Data1(out_6), .Read_Data2(out_7));
endmodule

module Control_Unit (
  input  [2:0] OpCode,
  output [2:0] ALUop,
  output ALUSrc,
  output RegDest,
  output RegWrite,
  output MemToReg,
  output MemRead,
  output MemWrite,
  output Jump,
  output Branch
);

  wire and_2_out, and_3_out, and_4_out, and_5_out, and_6_out, and_7_out, not_1_out, not_2_out, not_3_out;

  not not_1 (not_1_out, OpCode[2]);
  not not_2 (not_2_out, OpCode[1]);
  not not_3 (not_3_out, OpCode[0]);
  and and_1 (ALUop[2], OpCode[1], OpCode[0]);
  and and_2 (and_2_out, not_1_out, OpCode[0]);
  and and_3 (and_3_out, OpCode[2], OpCode[1]);
  and and_4 (and_4_out, not_1_out, OpCode[1], not_3_out);
  and and_5 (and_5_out, OpCode[2], not_2_out);
  and and_6 (and_6_out, OpCode[1], not_3_out);
  and and_7 (and_7_out, not_2_out, not_3_out);
  and and_8 (MemRead, OpCode[2], not_2_out, not_3_out);
  and and_9 (MemWrite, OpCode[2], not_2_out, OpCode[0]);
  and and_10 (Jump, OpCode[2], OpCode[1], OpCode[0]);
  and and_11 (Branch, OpCode[2], OpCode[1], not_3_out);
  or or_1 (ALUop[0], and_2_out, and_3_out);
  or or_2 (ALUSrc, and_4_out, and_5_out);
  or or_3 (RegDest, and_6_out, OpCode[2]);
  or or_4 (RegWrite, not_1_out, and_7_out);

  assign ALUop[1] = 1'b0;
  assign MemToReg = OpCode[2];

  // Notes on the sheet:
  //   Design of Control Unit
endmodule
